# Fritzing sketch led_pots_one_colour (saved by Fritzing 0.9.2b)
breadboards: 1

parts:
  VCC1 = Battery block 9V
  R1 = Resistor [tolerance=±5% resistance=220 package=THT]
  R4 = Rotary Potentiometer (Small) [maximum_resistance=100kΩ package=THT]
  LED1 = RGB LED (com. cathode, rbg) [package="5 mm [THT]"]

nets:
  N1: VCC1.-, R1.Pin_0, R4.leg1
  N2: VCC1.+, R4.leg2
  N3: R1.Pin_1, LED1.common_cathode
  N4: R4.wiper, LED1.red_anode
