# Fritzing sketch led_switch_threecolours (saved by Fritzing 0.9.2b)
breadboards: 1

parts:
  VCC1 = Battery block 9V
  LED1 = RGB LED (com. cathode, rgb) [package="5 mm [THT]"]
  R1 = Resistor [tolerance=±5% resistance=220 package=THT]
  S1 = Pushbutton [package=THT]
  S2 = Pushbutton [package=THT]
  S3 = Pushbutton [package=THT]

nets:
  N1: VCC1.-, R1.Pin_0
  N2: VCC1.+, S1.leg1, S2.leg1, S3.leg1
  N3: LED1.red_anode, S3.leg0
  N4: LED1.common_cathode, R1.Pin_1
  N5: LED1.green_anode, S2.leg0
  N6: LED1.blue_anode, S1.leg0

notes:
  The LONG pin in the coloured LED goes to black/blue/negative
  Put one resistor on the LONG pin, and the LED will be protected.
  Get ONE switch working first - plug it into each of the 3 pins to check all the colours work, then start to connect the other switches
